# Fritzing sketch bluefruit and button fritzing (saved by Fritzing 0.9.10b)

parts:
  Part1 = Adafruit Circuit Playground Bluefruit [part_number="Adafruit #4333"]
  S1 = Round Pushbutton

nets:
  N1: Part1.GND, S1.leg0
  N2: Part1.TX/D1, S1.leg1

custom parts:
  Adafruit Circuit Playground Bluefruit: Circuit Playground Bluefruit is our third board in the Circuit Playground series, another step towards a perfect introduction to electronics and programming. We've taken the popular Circuit Playground Express and made it even better! Now the main chip is an nRF52840 microcontroller which is not only more powerful, but also comes with Bluetooth Low Energy support for wireless connectivity. The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
